// Logisim project RAM - ukeoppgaver 5.circ as structural Verilog: 2 circuits, main circuit main
module main (
);

  _3a___RAM u_3a_ram_1 ();  // open: Adresse, Chip_select__0_disable_comp, Load__if_1___to_output, RESET__on_1, Data
  RAM #(.addrWidth(4), .dataWidth(4), .bus("asynch")) ram_1 ();  // open: addr, data, sel, ld, clr
endmodule

module _3a___RAM (
  input  [3:0] Adresse,
  input  Chip_select__0_disable_comp,
  input  Load__if_1___to_output,
  input  RESET__on_1,
  output [3:0] Data
);

  RAM #(.addrWidth(4), .dataWidth(4), .bus("asynch")) ram_1 (
    .addr(Adresse), .data(Data), .sel(Chip_select__0_disable_comp), .ld(Load__if_1___to_output),
    .clr(RESET__on_1));
endmodule
