// Logisim project uke9arkitektur.circ as structural Verilog: 8 circuits, main circuit main
module main (
  input  a0,
  input  a1,
  input  a2,
  input  a3,
  input  RESET,
  output [3:0] out_6
);

  wire clock_1_out;

  counter counter_1 (.CLK(clock_1_out), .\input ({a3, a2, a1, a0}), .out_4(out_6), .Reset(RESET));
  Clock clock_1 (.out(clock_1_out));
  // Probe on out_6
endmodule

// 4-bit Counter
module counter (
  input  Reset,
  input  CLK,
  input  [3:0] \input ,
  output [3:0] out_4
);

  wire [3:0] register_1_q;

  Register #(.width(4)) register_1 (.D(out_4), .Q(register_1_q), .clk(CLK), .clr(Reset));  // open: en
  _4_bits_adder u_4_bits_adder_1 (
    .a0(register_1_q[0]), .b0(\input [0]), .a1(register_1_q[1]), .b1(\input [1]), .a2(register_1_q[2]),
    .b2(\input [2]), .a3(register_1_q[3]), .b3(\input [3]), .s1(out_4[0]), .s2(out_4[1]), .s3(out_4[2]),
    .s4(out_4[3]));  // open: Carry
endmodule

// 4-bit adder
module _4_bits_adder (
  input  a0,
  input  b0,
  input  a1,
  input  b1,
  input  a2,
  input  b2,
  input  a3,
  input  b3,
  output s1,
  output s2,
  output s3,
  output s4,
  output Carry
);

  wire fulladder_1_c_1, fulladder_2_c_1, halfadder_1_c;

  Halfadder halfadder_1 (.A(a0), .B(b0), .S(s1), .C(halfadder_1_c));
  Fulladder fulladder_1 (.C(halfadder_1_c), .A(a1), .B(b1), .S_n(s2), .C_1(fulladder_1_c_1));
  Fulladder fulladder_2 (.C(fulladder_1_c_1), .A(a2), .B(b2), .S_n(s3), .C_1(fulladder_2_c_1));
  Fulladder fulladder_3 (.C(fulladder_2_c_1), .A(a3), .B(b3), .S_n(s4), .C_1(Carry));
endmodule

// 4b register
module _4_bit_register (
  input  [3:0] D_in,
  input  Clock,
  input  RESET,
  output [3:0] out_4
);

  D_Flipflop d_flipflop_1 (.D(Clock), .Clk(Clock), .ACLEAR(RESET), .out_4(out_4[0]));
  D_Flipflop d_flipflop_2 (.D(D_in[1]), .Clk(Clock), .ACLEAR(RESET), .out_4(out_4[1]));
  D_Flipflop d_flipflop_3 (.D(D_in[2]), .Clk(Clock), .ACLEAR(RESET), .out_4(out_4[2]));
  D_Flipflop d_flipflop_4 (.D(D_in[3]), .Clk(Clock), .ACLEAR(RESET), .out_4(out_4[3]));

  assign D_in[0] = Clock;
endmodule

module D_latch (
  input  D,
  input  CLK,
  output Q
);

  wire nand_1_out, nand_2_out, nand_4_out, not_1_out;

  not not_1 (not_1_out, D);
  nand nand_1 (nand_1_out, D, CLK);
  nand nand_2 (nand_2_out, not_1_out, CLK);
  nand nand_3 (Q, nand_1_out, nand_4_out);
  nand nand_4 (nand_4_out, Q, nand_2_out);
endmodule

module D_Flipflop (
  input  D,
  input  Clk,
  input  ACLEAR,
  output out_4
);

  wire and_1_out, d_latch_1_q, d_latch_2_q, not_1_out, not_2_out;

  D_latch d_latch_1 (.D(D), .CLK(Clk), .Q(d_latch_1_q));
  not not_1 (not_1_out, Clk);
  D_latch d_latch_2 (.D(d_latch_1_q), .CLK(not_1_out), .Q(d_latch_2_q));
  and and_1 (and_1_out, d_latch_2_q, ACLEAR);
  and and_2 (out_4, d_latch_2_q, not_2_out);
  not not_2 (not_2_out, and_1_out);
endmodule

// FA
module Fulladder (
  input  C,
  input  A,
  input  B,
  output S_n,
  output C_1
);

  wire and_1_out, halfadder_1_c, halfadder_1_s;

  Halfadder halfadder_1 (.A(A), .B(B), .S(halfadder_1_s), .C(halfadder_1_c));
  xor xor_1 (S_n, halfadder_1_s, C);
  and and_1 (and_1_out, halfadder_1_s, C);
  or or_1 (C_1, and_1_out, halfadder_1_c);
endmodule

// HA
module Halfadder (
  input  A,
  input  B,
  output S,
  output C
);

  xor xor_1 (S, A, B);
  and and_1 (C, A, B);
endmodule
