// Logisim project MiniCPU.circ as structural Verilog: 5 circuits, main circuit main
module main (
  input  Reset_Btn
);

  wire and_1_out, Clk, I1, I2, instruction_decoder_1_load_r_a, instruction_decoder_1_write_r_a, not_1_out,
       or_1_out;
  wire [3:0] Adresse, controlled_buffer_1_out, controlled_buffer_2_out, instruksjons_peker_1_out_3;
  wire [7:0] O, R_q;
  wire [7:4] ram_1_data;

  or or_1 (or_1_out, I2, I1);
  Clock Clock (.out(Clk));
  Register R (.D(O), .en(or_1_out), .Q(R_q), .clk(Clk));  // open: clr
  RAM Dataminne (
    .Adresse(Adresse), .Chip_select__0_disable_comp(1'b1), .Clk(Clk), .RESET__on_1(1'b0),
    .Load_0___Write_1(and_1_out), .Output(O), .Input(R_q));
  Instruksjons_Peker instruksjons_peker_1 (.Clk(Clk), .RESET(Reset_Btn), .out_3(instruksjons_peker_1_out_3));
  assign controlled_buffer_1_out = I1 ? R_q[3:0] : 4'bz;  // Controlled_Buffer controlled_buffer_1
  // Probe on controlled_buffer_1_out
  assign controlled_buffer_2_out = I2 ? R_q[7:4] : 4'bz;  // Controlled_Buffer controlled_buffer_2
  // Probe on controlled_buffer_2_out
  Instruction_Decoder instruction_decoder_1 (
    .MSB(ram_1_data), .Load_LSB_D(I1), .Load_MSB_D(I2), .Load_R_A(instruction_decoder_1_load_r_a),
    .Write_R_A(instruction_decoder_1_write_r_a));
  RAM_part #(.addrWidth(4)) ram_1 (
    .addr(instruksjons_peker_1_out_3), .data({ram_1_data, Adresse}), .sel(1'b1), .clk(Clk), .ld(1'b1),
    .clr(1'b0));
  and and_1 (and_1_out, not_1_out, instruction_decoder_1_write_r_a);
  not not_1 (not_1_out, instruction_decoder_1_load_r_a);
endmodule

// RAM (4)
module RAM (
  input  [3:0] Adresse,
  input  Chip_select__0_disable_comp,
  input  [7:0] Input,
  input  Clk,
  input  RESET__on_1,
  input  Load_0___Write_1,
  output [7:0] Output
);

  wire not_1_out;

  RAM_part #(.addrWidth(4)) ram_1 (
    .addr(Adresse), .data(Output), .sel(Chip_select__0_disable_comp), .clk(Clk), .ld(not_1_out),
    .clr(RESET__on_1));
  assign Output = Load_0___Write_1 ? Input : 8'bz;  // Controlled_Buffer controlled_buffer_1
  not not_1 (not_1_out, Load_0___Write_1);
endmodule

// IP
module Instruksjons_Peker (
  input  Clk,
  input  RESET,
  output [3:0] out_3
);

  wire and_1_out, nand_1_out;

  nand nand_1 (nand_1_out, out_3[0], out_3[1], out_3[2], out_3[3]);
  and and_1 (and_1_out, nand_1_out, Clk);
  Counter counter_1 (.Clk(and_1_out), .Reset(RESET), .out_3(out_3));
endmodule

module Counter (
  input  Clk,
  input  Reset,
  output [3:0] out_3
);

  wire [3:0] adder_1_out;

  Register #(.width(4)) register_1 (.D(adder_1_out), .Q(out_3), .clk(Clk), .clr(Reset));  // open: en
  Adder #(.width(4)) adder_1 (.a(4'b0001), .b(out_3), .out(adder_1_out));  // open: cin, cout
endmodule

// IDecoder
module Instruction_Decoder (
  input  [3:0] MSB,
  output Write_R_A,
  output Load_R_A,
  output Load_MSB_D,
  output Load_LSB_D
);

  wire and_2_out, and_3_out, not_1_out, not_2_out, not_3_out, not_4_out, or_1_out, or_2_out, or_3_out;

  nor nor_1 (Load_LSB_D, not_1_out, or_1_out);
  or or_1 (or_1_out, MSB[0], MSB[1], MSB[2]);
  not not_1 (not_1_out, MSB[3]);
  and and_1 (Write_R_A, MSB[3], MSB[1], MSB[0], not_3_out);
  nor nor_2 (Load_R_A, or_3_out, not_4_out);
  nor nor_3 (Load_MSB_D, not_2_out, or_2_out);
  not not_2 (not_2_out, and_2_out);
  or or_2 (or_2_out, MSB[2], MSB[1]);
  and and_2 (and_2_out, MSB[0], MSB[3]);
  not not_3 (not_3_out, MSB[2]);
  not not_4 (not_4_out, and_3_out);
  or or_3 (or_3_out, MSB[2], MSB[0]);
  and and_3 (and_3_out, MSB[3], MSB[1]);
endmodule
